# Fritzing sketch Controller (saved by Fritzing 0.7.0b)
breadboards: 1

parts:
  Part3 = Thumb Joystick
  Arduino2 = Arduino
  Part4 = Bluetooth HC-05 Macho

nets:
  GND: Part3.GND, Arduino2.GND, Part4.GND
  N1: Part3.SEL, Arduino2.D4
  N2: Part3.HORZ, Arduino2.A4
  N3: Part3.VERT, Arduino2.A3
  VCC: Part3.VCC, Arduino2.3V3, Part4.VCC
  N4: Arduino2.D3, Part4.RXD
  N5: Arduino2.D2, Part4.TXD
