# Fritzing sketch Hovercraft (saved by Fritzing 0.7.0b)
breadboards: 1

parts:
  Arduino1 = Arduino
  J1 = Basic Servo
  J2 = Basic Servo
  servant_hovercraft = Bluetooth HC-06
  ESC1 = ESC
  ESC2 = ESC

nets:
  GND: Arduino1.GND, J1.gnd, J2.gnd, servant_hovercraft.GND, ESC1.Ground, ESC2.Ground
  N1: Arduino1.D10, ESC2.Controller
  N2: Arduino1.D9, ESC1.Controller
  N3: Arduino1.D5, J2.pulse
  N4: Arduino1.D4, J1.pulse
  N5: Arduino1.D3, servant_hovercraft.RXD
  N6: Arduino1.D2, servant_hovercraft.TXD
  3V3: Arduino1.3V3, servant_hovercraft.VCC
  VCC: J1.vcc, ESC2.5v
  VCC_2: J2.vcc, ESC1.5v
