# Fritzing sketch LightHouseMaster (saved by Fritzing 0.7.0b)
breadboards: 1

parts:
  R2 = Rotary Potentiometer (Large) [maximum_resistance=100kΩ package=THT]
  LED1 = Super Flux RGB LED (com. cathode)
  Part1 = Bluetooth HC-05 Macho
  Arduino1 = Arduino
  R3 = Resistor [tolerance=±5% resistance=220 package=THT]
  R4 = Resistor [tolerance=±5% resistance=220 package=THT]
  R5 = Resistor [tolerance=±5% resistance=220 package=THT]

nets:
  N1: R2.leg1, Arduino1.+5V
  N2: R2.wiper, Arduino1.A0
  GND: R2.leg2, LED1.common_cathode, Part1.GND, Arduino1.GND
  N3: LED1.red_anode, R3.Pin_1
  N4: LED1.blue_anode, R5.Pin_1
  N5: LED1.green_anode, R4.Pin_1
  N6: Part1.TXD, Arduino1.D2
  N7: Part1.RXD, Arduino1.D3
  VCC: Part1.VCC, Arduino1.3V3
  N8: Arduino1.D10, R3.Pin_0
  N9: Arduino1.D9, R4.Pin_0
  N10: Arduino1.D8, R5.Pin_0
