# Fritzing sketch LightHouseServant (saved by Fritzing 0.7.0b)
breadboards: 1

parts:
  LED1 = Super Flux RGB LED (com. cathode)
  Arduino1 = Arduino
  R3 = Resistor [tolerance=±5% resistance=220 package=THT]
  R4 = Resistor [tolerance=±5% resistance=220 package=THT]
  R5 = Resistor [tolerance=±5% resistance=220 package=THT]
  Part1 = Bluetooth HC-06

nets:
  N1: LED1.red_anode, R3.Pin_1
  N2: LED1.blue_anode, R5.Pin_1
  N3: LED1.green_anode, R4.Pin_1
  GND: LED1.common_cathode, Arduino1.GND, Part1.GND
  N4: Arduino1.D10, R3.Pin_0
  N5: Arduino1.D9, R4.Pin_0
  N6: Arduino1.D8, R5.Pin_0
  N7: Arduino1.D3, Part1.RXD
  N8: Arduino1.D2, Part1.TXD
  3V3: Arduino1.3V3, Part1.VCC
